# Fritzing sketch Car (saved by Fritzing 0.9.2b)

parts:
  S1 = H-Bridge with L298N
  Часть1 = Arduino Mega 2560 (Rev3)
  NRF24L1 = NRF24L01
  M1 = DC Motor
  M2 = DC Motor
  M3 = DC Motor
  VCC1 = 4 x AAA Battery Mount
  VCC2 = 4 x AAA Battery Mount
  U1 = Voltage Regulator - 3.3V [package="TO220 [THT]"]
  M4 = DC Motor

nets:
  GND: S1.GND, Часть1.GND, NRF24L1.GND, VCC1.-, U1.GND
  N1: S1.ENA, Часть1.D9_PWM
  N2: S1.IN1, Часть1.D2_PWM
  N3: S1.IN2, Часть1.D3_PWM
  N4: S1.IN3, Часть1.D4_PWM
  N5: S1.IN4, Часть1.D5_PWM
  N6: S1.ENB, Часть1.D10_PWM
  N7: S1.M1-01, M1.pin_2, M2.pin_2
  N8: S1.M1-02, M1.pin_1, M2.pin_1
  N9: S1.M2-01, M3.pin_1, M4.pin_1
  N10: S1.M2-02, M3.pin_2, M4.pin_2
  N11: Часть1.D8_PWM, NRF24L1.CSN
  N12: Часть1.VIN, VCC2.+, U1.input_voltage
  N13: Часть1.D7_PWM, NRF24L1.CE
  N14: NRF24L1.VCC, U1.output_voltage
  N15: VCC1.+, VCC2.-

custom parts:
  H-Bridge with L298N: h-bridge
  NRF24L01: NRF24L01 module
