# Fritzing sketch IMU (saved by Fritzing 0.9.2b)

parts:
  Часть1 = Arduino Leonardo (Rev3b)
  NRF24L1 = NRF24L01
  U1 = Voltage Regulator - 5V [package="TO220 [THT]"]
  Часть4 = Triple Axis Magnetometer - HMC5883 Breakout
  VCC1 = Battery block 9V

nets:
  N1: Часть1.3V3, U1.output_voltage
  5V: Часть1.5V, Часть4.VCC
  GND: Часть1.GND, NRF24L1.GND, U1.GND, Часть4.GND, VCC1.-
  N2: Часть1.VIN, U1.input_voltage, VCC1.+
  N3: Часть1.D8/A8, NRF24L1.CE
  N4: Часть1.D9_PWM/A9, NRF24L1.CSN
  N5: Часть1.SDA, Часть4.SDA
  N6: Часть1.SCL, Часть4.SCL

custom parts:
  NRF24L01: NRF24L01 module
